// Logisim project Design.circ as structural Verilog: 1 circuit, main circuit main
module main (
);

  wire nand_1_out, nand_2_out, nand_3_out, nor_1_out, nor_2_out, nor_3_out, nor_4_out, nor_5_out, nor_6_out,
       nor_7_out, not_1_out, not_2_out, not_3_out, not_4_out, undriven, undriven_2, undriven_3, undriven_4,
       undriven_5, undriven_6;

  not not_1 (not_1_out, undriven_2);
  not not_2 (not_2_out, undriven_6);
  nor nor_1 (nor_1_out, undriven_4, undriven_5);
  nand nand_1 (nand_1_out, undriven_6, undriven);
  nand nand_2 (nand_2_out, undriven_6, not_1_out);
  nor nor_2 (nor_2_out, undriven, undriven_3);
  nand nand_3 (nand_3_out, not_1_out, not_2_out);
  not not_3 (not_3_out, nor_1_out);
  not not_4 (not_4_out, nand_1_out);
  nor nor_3 (nor_3_out, not_1_out, not_4_out);
  nor nor_4 (nor_4_out, nand_2_out, nor_2_out);
  nor nor_5 (nor_5_out, nor_2_out, nand_3_out);
  nor nor_6 (nor_6_out, nor_3_out, nor_4_out);
  nor nor_7 (nor_7_out, nor_3_out, nor_5_out);
  // NOR_Gate nor_8 has open pins: in0=not_3_out, in1=nor_6_out, out=open
  // NOR_Gate nor_9 has open pins: in0=not_3_out, in1=nor_7_out, out=open

  // Notes on the sheet:
  //   T
  //   S0
  //   REQ
  //   s1
  //   RST
  //   S2
  //   n2
  //   n1
  //   n0
endmodule
